// Logisim project bcd.circ as structural Verilog: 1 circuit, main circuit implementation
module implementation (
  input  w3,
  input  w2,
  input  w1,
  input  w0,
  output a,
  output b,
  output c,
  output d,
  output e,
  output f,
  output g
);


  // Other names for the same wires on the sheet: at = a; bt = b; ct = c; dt = d; et = e; ft = f; gt = g; w0t = w0;
  //   w1t = w1; w2t = w2; w3t = w3
endmodule
