// Logisim project grey.circ as structural Verilog: 1 circuit, main circuit implementation
module implementation (
  input  x2,
  input  x1,
  input  x0,
  output y2,
  output y1,
  output y0
);


  // Other names for the same wires on the sheet: x0t = x0; x1t = x1; x2t = x2; y0t = y0; y1t = y1; y2t = y2
endmodule
