// Logisim project grey.circ as structural Verilog: 1 circuit, main circuit implementation
module implementation (
  input  x2,
  input  x1,
  input  x0,
  output y2,
  output y1,
  output y0
);

  wire and_1_out, and_2_out, and_3_out, and_4_out, not_1_out, not_2_out, not_3_out, not_4_out;

  not not_1 (not_1_out, x2);
  not not_2 (not_2_out, x1);
  not not_3 (not_3_out, x0);
  not not_4 (not_4_out, x1);
  and and_1 (and_1_out, x1, not_1_out);
  and and_2 (and_2_out, x2, not_2_out);
  and and_3 (and_3_out, x1, not_3_out);
  and and_4 (and_4_out, not_4_out, x0);
  or or_1 (y1, and_1_out, and_2_out);
  or or_2 (y0, and_3_out, and_4_out);

  assign y2 = x2;

  // Other names for the same wires on the sheet: x0t = x0; x1t = x1; y0t = y0; y1t = y1; x2t = x2; y2t = x2
endmodule
