// Logisim project shifter.circ as structural Verilog: 1 circuit, main circuit implementation
module implementation (
  input  IsRightShiftIn,
  input  IsArithmeticIn,
  input  [1:0] ShiftAmountIn,
  input  [2:0] NumberIn,
  output [2:0] ShiftedNumberOut
);


  // Other names for the same wires on the sheet: IsArithmetic = IsArithmeticIn; IsRightShift = IsRightShiftIn;
  //   Number[2:0] = NumberIn; ShiftAmount[1:0] = ShiftAmountIn; ShiftedNumber[2:0] = ShiftedNumberOut
endmodule
