// Logisim project UpDownCountergrader.circ as structural Verilog: 4 circuits, main circuit main
module main (
  input  StopOnMismatchIn,
  output [2:0] CountOut,
  output CountUpOut,
  output CountDownOut,
  output ClkOut,
  output halt
);

  wire and_1_out, not_1_out, StopTesting, StudentAnswerIsCorrect;
  wire [2:0] CorrectCount;
  wire [5:0] counter_1_q, TestNumber;

  Clock clock_1 (.out(ClkOut));
  input_generator input_generator_1 (
    .stop_testing_in(StopTesting), .clkin(ClkOut), .TestNumberOut(TestNumber), .CountUp(CountUpOut),
    .CountDown(CountDownOut), .DoneTestingOut(halt));
  // Probe on CountOut
  Counter #(.max('h21), .ongoal("stay"), .width(6)) counter_1 (
    .up(and_1_out), .count(and_1_out), .clk(ClkOut), .Q(counter_1_q));  // open: clr, load, D, carry
  and and_1 (and_1_out, StudentAnswerIsCorrect, ~halt, ~StopTesting);  // AND_Gate
  not not_1 (not_1_out, StopTesting);
  // Probe on TestNumber
  // Probe on StudentAnswerIsCorrect
  implementation implementation_1 (
    .EnableIn(not_1_out), .CountUpIn(CountUpOut), .CountDownIn(CountDownOut), .clkIn(ClkOut), .Count(CountOut));
  // Probe on CorrectCount
  // Probe on counter_1_q
  \checker  checker_1 (
    .CountUpIn(CountUpOut), .CountDownIn(CountDownOut), .StopOnMismatchIn(StopOnMismatchIn),
    .StudentCountIn(CountOut), .clkIn(ClkOut), .CorrectCountOut(CorrectCount),
    .StudentAnswerIsCorrectOut(StudentAnswerIsCorrect), .StopTestingOut(StopTesting));

  // Other names for the same wires on the sheet: clk = ClkOut; Count[2:0] = CountOut; CountUp = CountUpOut;
  //   CoutDown = CountDownOut; stop = halt; StopOnMismatch = StopOnMismatchIn

  // Notes on the sheet:
  //   SetStepOnMismatch to 1 to have the testing circuit stop on the first output that is incorrect
  //   Maximum Number Correct is 33
endmodule

module input_generator (
  input  stop_testing_in,
  input  clkin,
  output [5:0] TestNumberOut,
  output CountUp,
  output CountDown,
  output DoneTestingOut
);

  wire not_1_out;

  not not_1 (not_1_out, stop_testing_in);
  Counter #(.max('h21), .ongoal("stay"), .width(6)) counter_1 (
    .up(1'b1), .count(not_1_out), .clk(clkin), .carry(DoneTestingOut), .Q(TestNumberOut));  // open: clr, load, D
  ROM #(.addrWidth(6), .dataWidth(2)) rom_1 (.addr(TestNumberOut), .data({CountUp, CountDown}));

  // Other names for the same wires on the sheet: clk = clkin; done_testing = DoneTestingOut;
  //   stop_testing = stop_testing_in; TestNumber[5:0] = TestNumberOut

  // Notes on the sheet:
  //   contents of rom_1 (hex, n*v repeats v):
  //   0 2 0 2 0 2 0 2 0 2 0 2 0 2 0 2 0 1 0 1 0 1 0 1 0 1 0 1 0 1 0 1
endmodule

module \checker  (
  input  CountUpIn,
  input  CountDownIn,
  input  StopOnMismatchIn,
  input  [2:0] StudentCountIn,
  input  clkIn,
  output [2:0] CorrectCountOut,
  output StudentAnswerIsCorrectOut,
  output StopTestingOut
);

  wire and_1_out, and_3_out, CounterEnable, or_1_out, or_2_out;

  and and_1 (and_1_out, StudentAnswerIsCorrectOut, StopOnMismatchIn);
  or or_1 (or_1_out, CountUpIn, CountDownIn);
  or or_2 (or_2_out, ~StopOnMismatchIn, and_1_out);  // OR_Gate
  and and_2 (CounterEnable, or_1_out, or_2_out);
  and and_3 (and_3_out, CounterEnable, ~StopTestingOut);  // AND_Gate
  Counter #(.max('h7), .ongoal("stay"), .width(3)) counter_1 (
    .up(CountUpIn), .count(and_3_out), .clk(clkIn), .Q(CorrectCountOut));  // open: clr, load, D, carry
  stop_testing_circ stop_testing_circ_1 (
    .StopOnIncorrectIn(StopOnMismatchIn), .AnswerIsCorrectIn(StudentAnswerIsCorrectOut), .ClkIn(clkIn),
    .StopTestingOut(StopTestingOut));
  Comparator #(.width(3)) comparator_1 (
    .a(StudentCountIn), .b(CorrectCountOut), .eq(StudentAnswerIsCorrectOut));  // open: gt, lt

  // Other names for the same wires on the sheet: clk = clkIn; CorrectCount[2:0] = CorrectCountOut;
  //   CountDown = CountDownIn; CountUp = CountUpIn; StopOnMismatch = StopOnMismatchIn; StopTesting = StopTestingOut;
  //   StudentCount[2:0] = StudentCountIn; StudentCountIsCorrect = StudentAnswerIsCorrectOut
endmodule

module stop_testing_circ (
  input  StopOnIncorrectIn,
  input  AnswerIsCorrectIn,
  input  ClkIn,
  output StopTestingOut
);

  wire SavedStopTesting, StopTesting;

  and and_1 (StopTesting, ~AnswerIsCorrectIn, StopOnIncorrectIn);  // AND_Gate
  Register #(.width(1)) register_1 (.D(StopTesting), .en(StopTesting), .clk(ClkIn), .Q(SavedStopTesting));  // open: clr
  or or_1 (StopTestingOut, StopTesting, SavedStopTesting);

  // Other names for the same wires on the sheet: AnswerIsCorrect = AnswerIsCorrectIn; clk = ClkIn;
  //   StopOnIncorrect = StopOnIncorrectIn
endmodule
