// Logisim project FourBitParity.circ as structural Verilog: 28 circuits, main circuit implementation
module implementation (
  input  EnableIn,
  input  InputBitIn,
  input  ClkIn,
  output IsEvenOut
);

  wire register_1_q;

  Register #(.width(1)) register_1 (.D(InputBitIn), .en(EnableIn), .clk(ClkIn), .Q(register_1_q));  // open: clr
  Five five_1 (.Input(register_1_q), .IsEvenOut(IsEvenOut));

  // Other names for the same wires on the sheet: Clk = ClkIn; Enable = EnableIn; InputBit = InputBitIn;
  //   IsEven = IsEvenOut
endmodule

module Next_S3 (
  input  S3,
  input  S2,
  input  S1,
  input  S0,
  input  Bit_inp,
  input  Enable,
  output S3_next
);

  and and_1 (S3_next, S2, Enable);
endmodule

module Next_S2 (
  input  S3,
  input  S2,
  input  S1,
  input  S0,
  input  BIT,
  input  Enable,
  output S2_NEXT
);

  wire and_1_out, and_2_out, not_1_out, not_2_out;

  not not_1 (not_1_out, S3);
  not not_2 (not_2_out, S0);
  and and_1 (and_1_out, not_1_out, not_2_out, Enable);
  and and_2 (and_2_out, not_1_out, S1, Enable);
  or or_1 (S2_NEXT, and_1_out, and_2_out);
endmodule

module NEXT_S1 (
  input  S3,
  input  S2,
  input  S1,
  input  S0,
  input  BIT,
  input  Enable,
  output S1_NEXT
);

  wire and_1_out, and_2_out, and_3_out, and_4_out, not_1_out, not_2_out, not_3_out, not_4_out;

  not not_1 (not_1_out, S3);
  not not_2 (not_2_out, S2);
  not not_3 (not_3_out, S0);
  not not_4 (not_4_out, BIT);
  and and_1 (and_1_out, not_1_out, not_2_out, not_3_out, not_4_out, Enable);
  and and_2 (and_2_out, S2, S0, not_4_out, Enable);
  and and_3 (and_3_out, not_2_out, S0, BIT, Enable);
  and and_4 (and_4_out, S3, not_2_out, BIT, Enable);
  or or_1 (S1_NEXT, and_1_out, and_2_out, and_3_out, and_4_out);
endmodule

module NEXT_S0 (
  input  S3,
  input  S2,
  input  S1,
  input  S0,
  input  BIT,
  input  Enable,
  output S0_NEXT
);

  wire and_1_out, and_2_out, and_3_out, and_4_out, and_5_out, not_1_out, not_2_out, not_3_out, not_4_out,
       not_5_out;

  not not_1 (not_1_out, S3);
  not not_2 (not_2_out, S2);
  not not_3 (not_3_out, S1);
  not not_4 (not_4_out, S0);
  not not_5 (not_5_out, BIT);
  and and_1 (and_1_out, not_1_out, not_2_out, not_4_out, not_5_out, Enable);
  and and_2 (and_2_out, S2, S0, not_5_out, Enable);
  and and_3 (and_3_out, not_2_out, S0, BIT, Enable);
  and and_4 (and_4_out, S3, not_2_out, BIT, Enable);
  and and_5 (and_5_out, S2, not_3_out, BIT, Enable);
  or or_1 (S0_NEXT, and_1_out, and_2_out, and_3_out, and_4_out, and_5_out);
endmodule

module Next_stat_eqs (
  input  BIT_INP,
  input  [3:0] STATE,
  input  Enable,
  output S3_NEXT,
  output S2_NEXT,
  output S1_NEXT,
  output S0_NEXT
);

  Next_S3 next_s3_1 (
    .S3(STATE[3]), .S2(STATE[2]), .S1(STATE[1]), .S0(STATE[0]), .Bit_inp(BIT_INP), .Enable(Enable),
    .S3_next(S3_NEXT));
  Next_S2 next_s2_1 (
    .S3(STATE[3]), .S2(STATE[2]), .S1(STATE[1]), .S0(STATE[0]), .BIT(BIT_INP), .Enable(Enable),
    .S2_NEXT(S2_NEXT));
  NEXT_S1 next_s1_1 (
    .S3(STATE[3]), .S2(STATE[2]), .S1(STATE[1]), .S0(STATE[0]), .BIT(BIT_INP), .Enable(Enable),
    .S1_NEXT(S1_NEXT));
  NEXT_S0 next_s0_1 (
    .S3(STATE[3]), .S2(STATE[2]), .S1(STATE[1]), .S0(STATE[0]), .BIT(BIT_INP), .Enable(Enable),
    .S0_NEXT(S0_NEXT));

  // Other names for the same wires on the sheet: S0 = STATE[0]; S1 = STATE[1]; S2 = STATE[2]; S3 = STATE[3]
endmodule

module STATE_CIR (
  input  ClkIn,
  input  S3_n,
  input  s2_n,
  input  s1_n,
  input  s0_n,
  output [3:0] STATE
);

  D_Flip_Flop d_ff_1 (.D(S3_n), .clk(ClkIn), .Q(STATE[3]));  // open: Qn, preset, reset
  D_Flip_Flop d_ff_2 (.D(s2_n), .clk(ClkIn), .Q(STATE[2]));  // open: Qn, preset, reset
  D_Flip_Flop d_ff_3 (.D(s1_n), .clk(ClkIn), .Q(STATE[1]));  // open: Qn, preset, reset
  D_Flip_Flop d_ff_4 (.D(s0_n), .clk(ClkIn), .Q(STATE[0]));  // open: Qn, preset, reset

  // Other names for the same wires on the sheet: Clk = ClkIn; S0 = STATE[0]; S1 = STATE[1]; S2 = STATE[2];
  //   S3 = STATE[3]
endmodule

module IFEVEN (
  input  BIT_INP,
  input  ClkIn,
  input  Enable,
  output ISEVEN
);

  wire next_stat_eqs_1_s0_next, next_stat_eqs_1_s1_next, next_stat_eqs_1_s2_next, next_stat_eqs_1_s3_next;
  wire [3:0] STATE, state_cir_1_state;

  Next_stat_eqs next_stat_eqs_1 (
    .BIT_INP(BIT_INP), .STATE(STATE), .Enable(Enable), .S3_NEXT(next_stat_eqs_1_s3_next),
    .S2_NEXT(next_stat_eqs_1_s2_next), .S1_NEXT(next_stat_eqs_1_s1_next), .S0_NEXT(next_stat_eqs_1_s0_next));
  STATE_CIR state_cir_1 (
    .ClkIn(ClkIn), .S3_n(next_stat_eqs_1_s3_next), .s2_n(next_stat_eqs_1_s2_next),
    .s1_n(next_stat_eqs_1_s1_next), .s0_n(next_stat_eqs_1_s0_next), .STATE(state_cir_1_state));
  maybe maybe_1 (
    .Enable(Enable), .S3(state_cir_1_state[3]), .S2(state_cir_1_state[2]), .S1(state_cir_1_state[1]),
    .S0(state_cir_1_state[0]), .IS_EVEN(ISEVEN));

  // Other names for the same wires on the sheet: Clk = ClkIn
endmodule

module maybe (
  input  Enable,
  input  S3,
  input  S2,
  input  S1,
  input  S0,
  output IS_EVEN
);

  wire not_1_out;

  not not_1 (not_1_out, S2);
  and and_1 (IS_EVEN, S3, not_1_out, S1, Enable);
endmodule

module two (
  input  [2:0] curr_stae,
  input  EnableIn,
  input  ClkIn,
  output [2:0] next_stat
);

  Register #(.width(3)) register_1 (.D(curr_stae), .en(EnableIn), .clk(ClkIn), .Q(next_stat));  // open: clr
endmodule

module two_further (
  input  InputBitIn,
  input  [2:0] curr_stat,
  output [2:0] next_stat
);

  wire and_1_out, and_2_out, and_3_out, and_4_out, and_5_out, and_6_out, not_1_out, not_2_out, not_4_out;

  not not_1 (not_1_out, InputBitIn);
  not not_2 (not_2_out, curr_stat[2]);
  not not_3 (next_stat[1], curr_stat[1]);
  not not_4 (not_4_out, curr_stat[0]);
  and and_1 (and_1_out, not_2_out, curr_stat[1]);
  and and_2 (and_2_out, curr_stat[2], next_stat[1]);
  and and_3 (and_3_out, not_1_out, not_2_out, curr_stat[0]);
  and and_4 (and_4_out, not_1_out, next_stat[1], curr_stat[0]);
  and and_5 (and_5_out, InputBitIn, not_4_out);
  and and_6 (and_6_out, InputBitIn, curr_stat[2], curr_stat[1]);
  or or_1 (next_stat[2], and_1_out, and_2_out);
  or or_2 (next_stat[0], and_3_out, and_4_out, and_5_out, and_6_out);

  // Other names for the same wires on the sheet: InputBit = InputBitIn
endmodule

module two_ev (
  input  EnableIn,
  input  InputBitIn,
  input  ClkIn,
  output IS_Even
);

  wire [2:0] curr_sta, two_further_1_next_stat;

  two_further two_further_1 (.InputBitIn(InputBitIn), .curr_stat(curr_sta), .next_stat(two_further_1_next_stat));
  two two_1 (.curr_stae(two_further_1_next_stat), .EnableIn(EnableIn), .ClkIn(ClkIn), .next_stat(curr_sta));
  two_if two_if_1 (.stat(curr_sta), .evn(IS_Even));

  // Other names for the same wires on the sheet: Clk = ClkIn; Enable = EnableIn; InputBit = InputBitIn
endmodule

module two_if (
  input  [2:0] stat,
  output evn
);

  wire not_1_out;

  not not_1 (not_1_out, stat[0]);
  and and_1 (evn, stat[2], stat[1], not_1_out);
endmodule

module THREE_s2 (
  input  S2,
  input  S1,
  input  S0,
  input  BIT,
  output NEXT_S2
);


  assign NEXT_S2 = S1;
endmodule

module THREE_S1 (
  input  S2,
  input  S1,
  input  S0,
  input  BIT,
  output NEXT_S1
);

  not not_1 (NEXT_S1, S2);
endmodule

module THREE_S0 (
  input  S2,
  input  S1,
  input  S0,
  input  BIT,
  output NEXT_S0
);

  wire and_1_out, and_2_out, and_3_out, and_4_out, and_5_out, not_1_out, not_2_out, not_3_out, not_4_out;

  not not_1 (not_1_out, S2);
  not not_2 (not_2_out, S1);
  not not_3 (not_3_out, S0);
  not not_4 (not_4_out, BIT);
  and and_1 (and_1_out, not_1_out, not_2_out, S0, not_4_out);
  and and_2 (and_2_out, S1, S0, not_4_out);
  and and_3 (and_3_out, not_1_out, not_2_out, S0, BIT);
  and and_4 (and_4_out, S1, not_3_out, BIT);
  and and_5 (and_5_out, S2, not_2_out, BIT);
  or or_1 (NEXT_S0, and_1_out, and_2_out, and_3_out, and_4_out, and_5_out);
endmodule

module THREE_STATE_CIRC (
  input  ClkIn,
  input  EnableIn,
  input  S2NEXT,
  input  S1NEXT,
  input  S0NEXT,
  output [2:0] State
);

  Register #(.width(1)) register_1 (.D(S2NEXT), .en(EnableIn), .clk(ClkIn));  // open: Q, clr
  Register #(.width(1)) register_2 (.D(S1NEXT), .en(EnableIn), .clk(ClkIn));  // open: Q, clr
  Register #(.width(1)) register_3 (.D(S0NEXT), .en(EnableIn), .clk(ClkIn));  // open: Q, clr

  // Other names for the same wires on the sheet: Clk = ClkIn; Enable = EnableIn; S2 = State[0]; S1 = State[1];
  //   S0 = State[2]
endmodule

module THREE_NEXTSTATE (
  input  BitInputIn,
  input  [2:0] StateIn,
  output S2Next,
  output S1Next,
  output S0Next
);

  THREE_s2 three_s2_1 (.S2(StateIn[2]), .S1(StateIn[1]), .S0(StateIn[0]), .BIT(BitInputIn), .NEXT_S2(S2Next));
  THREE_S1 three_s1_1 (.S2(StateIn[2]), .S1(StateIn[1]), .S0(StateIn[0]), .BIT(BitInputIn), .NEXT_S1(S1Next));
  THREE_S0 three_s0_1 (.S2(StateIn[2]), .S1(StateIn[1]), .S0(StateIn[0]), .BIT(BitInputIn), .NEXT_S0(S0Next));

  // Other names for the same wires on the sheet: BitInput = BitInputIn; State[2:0] = StateIn
endmodule

module threeFsm_cir (
  input  EnableIn,
  input  InputBitIn,
  input  ClkIn,
  output EVEN_PAR
);

  wire three_nextstate_1_s0next, three_nextstate_1_s1next, three_nextstate_1_s2next;
  wire [2:0] State;

  THREE_NEXTSTATE three_nextstate_1 (
    .BitInputIn(InputBitIn), .StateIn(State), .S2Next(three_nextstate_1_s2next),
    .S1Next(three_nextstate_1_s1next), .S0Next(three_nextstate_1_s0next));
  THREE_STATE_CIRC three_state_circ_1 (
    .ClkIn(ClkIn), .EnableIn(EnableIn), .S2NEXT(three_nextstate_1_s2next), .S1NEXT(three_nextstate_1_s1next),
    .S0NEXT(three_nextstate_1_s0next), .State(State));
  three_outputeqs three_outputeqs_1 (.S2(State[2]), .S1(State[1]), .S0(State[0]), .EVEN_PAR(EVEN_PAR));

  // Other names for the same wires on the sheet: Clk = ClkIn; Enable = EnableIn; InputBit = InputBitIn
endmodule

module three_outputeqs (
  input  S2,
  input  S1,
  input  S0,
  output EVEN_PAR
);

  wire not_1_out;

  not not_1 (not_1_out, S1);
  and and_1 (EVEN_PAR, S2, not_1_out, S0);
endmodule

module FOUR_S2 (
  input  S2,
  input  S1,
  input  S0,
  input  Enable,
  output NEXT_S2
);

  wire and_1_out, and_2_out;

  and and_1 (and_1_out, S1, Enable);
  and and_2 (and_2_out, S2, Enable);
  or or_1 (NEXT_S2, and_1_out, and_2_out);
endmodule

module four_s0 (
  input  S2,
  input  S1,
  input  S0,
  input  BIT,
  output NEXT_S0
);

  wire and_1_out, and_2_out, and_3_out, and_4_out, and_5_out, and_6_out, and_7_out, not_1_out, not_2_out,
       not_3_out, not_4_out;

  not not_1 (not_1_out, S2);
  not not_2 (not_2_out, S1);
  not not_3 (not_3_out, S0);
  not not_4 (not_4_out, BIT);
  and and_1 (and_1_out, not_1_out, not_2_out, S0, not_4_out);
  and and_2 (and_2_out, S1, S0, not_4_out);
  and and_3 (and_3_out, S2, S0, not_4_out);
  and and_4 (and_4_out, not_1_out, not_2_out, S0, BIT);
  and and_5 (and_5_out, S1, not_3_out, BIT);
  and and_6 (and_6_out, S2, not_2_out, BIT);
  and and_7 (and_7_out, S2, not_2_out, BIT);
  or or_1 (NEXT_S0, and_1_out, and_2_out, and_3_out, and_4_out, and_5_out, and_6_out, and_7_out);
endmodule

module Four_nextstae (
  input  BitInputIn,
  input  [2:0] StateIn,
  output S2Next,
  output S1Next,
  output S0Next
);

  THREE_S1 three_s1_1 (.S2(StateIn[2]), .S1(StateIn[1]), .S0(StateIn[0]), .BIT(BitInputIn), .NEXT_S1(S1Next));
  THREE_S0 three_s0_1 (.S2(StateIn[2]), .S1(StateIn[1]), .S0(StateIn[0]), .BIT(BitInputIn), .NEXT_S0(S0Next));

  // Other names for the same wires on the sheet: BitInput = BitInputIn; State[2:0] = StateIn
endmodule

module Five (
  input  Input,
  output IsEvenOut
);

  wire and_1_out, and_2_out, and_3_out, and_4_out, and_5_out, and_6_out, not_1_out, not_3_out, not_4_out;
  wire [2:0] curr_state, next_state;

  not not_1 (not_1_out, curr_state[2]);
  not not_2 (next_state[1], curr_state[1]);
  not not_3 (not_3_out, curr_state[0]);
  not not_4 (not_4_out, Input);
  and and_1 (and_1_out, not_1_out, curr_state[1]);
  or or_1 (next_state[2], and_1_out, and_2_out);
  and and_2 (and_2_out, curr_state[2], next_state[1]);
  and and_3 (and_3_out, not_3_out, Input);
  and and_4 (and_4_out, not_1_out, curr_state[0], not_4_out);
  and and_5 (and_5_out, next_state[1], curr_state[0], not_4_out);
  and and_6 (and_6_out, curr_state[2], curr_state[1], Input);
  and and_7 (IsEvenOut, curr_state[2], curr_state[1], not_3_out);
  or or_2 (next_state[0], and_3_out, and_4_out, and_5_out, and_6_out);
endmodule

module five_next (
  input  EnableIn,
  input  InputBitIn,
  input  ClkIn,
  output Iseven
);

  wire five_1_isevenout;
  wire [2:0] state;

  Register #(.width(1)) register_1 (.D(InputBitIn));  // open: en, clk, Q, clr
  Five five_1 (.IsEvenOut(five_1_isevenout));  // open: Input
  Register #(.width(3)) register_2 (.en(EnableIn), .clk(ClkIn), .Q(state));  // open: D, clr
  five_next2 five_next2_1 (.state(state), .isEven(Iseven));

  // Other names for the same wires on the sheet: Clk = ClkIn; Enable = EnableIn; InputBit = InputBitIn
endmodule

module five_next2 (
  input  [2:0] state,
  output isEven
);

  wire not_1_out;

  not not_1 (not_1_out, state[0]);
  and and_1 (isEven, state[2], state[1], not_1_out);
endmodule

module five_final (
  input  EnableIn,
  input  InputBitIn,
  input  ClkIn,
  output IsEvenOut
);

  wire [2:0] five_1_p1, five_1_p3;

  // Five five_1: pin names not known; wires that end beside it: five_1_p1, InputBitIn, five_1_p3
  Register #(.width(3)) register_1 (.D(five_1_p3), .en(EnableIn), .clk(ClkIn), .Q(five_1_p1));  // open: clr
  five_next3 five_next3_1 (.curr_state(five_1_p1), .IsEvenOut(IsEvenOut));

  // Other names for the same wires on the sheet: Clk = ClkIn; Enable = EnableIn; InputBit = InputBitIn
endmodule

module five_next3 (
  input  [2:0] curr_state,
  output IsEvenOut
);

  wire not_1_out, not_2_out;

  not not_1 (not_1_out, curr_state[2]);
  not not_2 (not_2_out, curr_state[1]);
  and and_1 (IsEvenOut, not_1_out, not_2_out);
endmodule
