// Logisim project UpDownCounter.circ as structural Verilog: 4 circuits, main circuit implementation
module implementation (
  input  EnableIn,
  input  CountUpIn,
  input  CountDownIn,
  input  clkIn,
  output [2:0] Count
);

  wire [2:0] nextstatecirc_1_nextcount;

  NextStateCirc nextstatecirc_1 (
    .CurCount(Count), .CountUp(CountUpIn), .CountDown(CountDownIn), .NextCount(nextstatecirc_1_nextcount));
  Register #(.width(3)) register_1 (.D(nextstatecirc_1_nextcount), .en(EnableIn), .clk(clkIn), .Q(Count));  // open: clr

  // Other names for the same wires on the sheet: CL = clkIn; COu[2:0] = Count; Down = CountDownIn; Ena = EnableIn;
  //   UP = CountUpIn
endmodule

module NextStateCirc (
  input  [2:0] CurCount,
  input  CountUp,
  input  CountDown,
  output [2:0] NextCount
);

  wire and_1_out, and_2_out, and_3_out, and_4_out, and_5_out, and_6_out, and_7_out, and_8_out, and_9_out,
       and_10_out, and_11_out, and_12_out, and_13_out, and_14_out, and_15_out, and_16_out, and_17_out,
       and_18_out, not_1_out, not_2_out, not_3_out, not_4_out, not_5_out;

  not not_1 (not_1_out, CurCount[2]);
  not not_2 (not_2_out, CurCount[1]);
  not not_3 (not_3_out, CurCount[0]);
  not not_4 (not_4_out, CountUp);
  not not_5 (not_5_out, CountDown);
  and and_1 (and_1_out, CurCount[1], CurCount[0], CountUp, not_5_out);
  and and_2 (and_2_out, CurCount[2], not_5_out);
  and and_3 (and_3_out, CurCount[2], CountUp);
  and and_4 (and_4_out, CurCount[2], CurCount[0]);
  and and_5 (and_5_out, CurCount[2], CurCount[1]);
  and and_6 (and_6_out, not_2_out, CurCount[0], CountUp);
  and and_7 (and_7_out, CurCount[1], not_3_out, not_5_out);
  and and_8 (and_8_out, CurCount[1], not_3_out, CountUp);
  and and_9 (and_9_out, CurCount[1], CurCount[0], not_4_out);
  and and_10 (and_10_out, not_1_out, CurCount[1], CurCount[0], CountDown);
  and and_11 (and_11_out, CurCount[2], not_2_out, not_3_out, not_4_out, CountDown);
  and and_12 (and_12_out, CurCount[2], CurCount[1], not_5_out);
  and and_13 (and_13_out, not_3_out, CountUp);
  and and_14 (and_14_out, CurCount[0], not_4_out, not_5_out);
  and and_15 (and_15_out, CurCount[1], not_3_out, CountDown);
  and and_16 (and_16_out, not_1_out, CurCount[1], CountUp, CountDown);
  and and_17 (and_17_out, CurCount[2], not_3_out, CountDown);
  and and_18 (and_18_out, CurCount[2], CurCount[1], CurCount[0], not_5_out);
  or or_1 (NextCount[2], and_1_out, and_2_out, and_3_out, and_4_out, and_5_out);
  or or_2 (NextCount[1], and_6_out, and_7_out, and_8_out, and_9_out, and_10_out, and_11_out, and_12_out);
  or or_3 (NextCount[0], and_13_out, and_14_out, and_15_out, and_16_out, and_17_out, and_18_out);
endmodule

module NextStateAdd (
  input  [2:0] Curr_state,
  output [2:0] Next_State
);

  wire and_1_out, and_2_out, and_3_out, and_4_out, and_5_out, not_1_out, not_2_out;

  not not_1 (not_1_out, Curr_state[1]);
  not not_2 (not_2_out, Curr_state[0]);
  and and_1 (and_1_out, Curr_state[1], Curr_state[0]);
  and and_2 (and_2_out, not_1_out, Curr_state[0]);
  and and_3 (and_3_out, Curr_state[1], not_2_out);
  and and_4 (and_4_out, Curr_state[2], Curr_state[1]);
  and and_5 (and_5_out, Curr_state[2], Curr_state[1]);
  or or_1 (Next_State[2], and_1_out, Curr_state[2]);
  or or_2 (Next_State[1], and_2_out, and_3_out, and_4_out);
  or or_3 (Next_State[0], not_2_out, and_5_out);
endmodule

module NextStateDown (
  input  [2:0] curr_state,
  output [2:0] next_state
);

  wire and_1_out, and_2_out, and_3_out, and_4_out, and_5_out, and_6_out, not_1_out, not_2_out;

  not not_1 (not_1_out, curr_state[1]);
  not not_2 (not_2_out, curr_state[0]);
  and and_1 (and_1_out, curr_state[2], curr_state[0]);
  and and_2 (and_2_out, curr_state[2], curr_state[1]);
  and and_3 (and_3_out, curr_state[1], curr_state[0]);
  and and_4 (and_4_out, curr_state[2], not_1_out, not_2_out);
  and and_5 (and_5_out, curr_state[1], not_2_out);
  and and_6 (and_6_out, curr_state[2], not_2_out);
  or or_1 (next_state[2], and_1_out, and_2_out);
  or or_2 (next_state[1], and_3_out, and_4_out);
  or or_3 (next_state[0], and_5_out, and_6_out);
endmodule
