// Logisim project Vending.circ as structural Verilog: 2 circuits, main circuit implementation
module implementation (
  input  EnableIn,
  input  QuarterReceivedIn,
  input  DimeReceivedIn,
  input  NickelReceivedIn,
  input  ClkIn,
  output Give_Mechandise_Out,
  output Give_Dime_Out,
  output Give_Nickel_Out
);

  eqs eqs_1 (
    .EnableIn(EnableIn), .QuarterReceivedIn(QuarterReceivedIn), .DimeReceivedIn(DimeReceivedIn),
    .NickelReceivedIn(NickelReceivedIn), .ClkIn(ClkIn), .dispense(Give_Mechandise_Out),
    .dime_out(Give_Dime_Out), .nickel_out(Give_Nickel_Out));

  // Other names for the same wires on the sheet: clk = ClkIn; DimeReceieved = DimeReceivedIn; Enable = EnableIn;
  //   Give_Dime = Give_Dime_Out; Give_Merchandise = Give_Mechandise_Out; Give_Nickel = Give_Nickel_Out;
  //   NickelReceieved = NickelReceivedIn; QuarterReceieved = QuarterReceivedIn
endmodule

module eqs (
  input  EnableIn,
  input  QuarterReceivedIn,
  input  DimeReceivedIn,
  input  NickelReceivedIn,
  input  ClkIn,
  output dispense,
  output dime_out,
  output nickel_out
);

  wire and_1_out, and_2_out, and_3_out, and_4_out, and_5_out, and_6_out, and_7_out, and_8_out, and_9_out,
       and_10_out, and_11_out, and_12_out, and_13_out, and_14_out, and_15_out, and_16_out, and_17_out,
       and_18_out, and_19_out, and_20_out, and_21_out, and_22_out, and_23_out, and_24_out, and_25_out,
       not_1_out, not_2_out, not_3_out, not_4_out, not_5_out, not_6_out, register_1_q, register_2_q,
       register_3_q;
  wire [2:0] curr_state, next_state;

  Register #(.width(1)) register_1 (.D(QuarterReceivedIn), .en(EnableIn), .clk(ClkIn), .Q(register_1_q));  // open: clr
  Register #(.width(1)) register_2 (.D(DimeReceivedIn), .en(EnableIn), .clk(ClkIn), .Q(register_2_q));  // open: clr
  Register #(.width(1)) register_3 (.D(NickelReceivedIn), .en(EnableIn), .clk(ClkIn), .Q(register_3_q));  // open: clr
  not not_1 (not_1_out, curr_state[2]);
  not not_2 (not_2_out, curr_state[1]);
  not not_3 (not_3_out, curr_state[0]);
  not not_4 (not_4_out, register_1_q);
  not not_5 (not_5_out, register_2_q);
  not not_6 (not_6_out, register_3_q);
  and and_1 (and_1_out, not_1_out, not_2_out, not_3_out, register_1_q);
  and and_2 (and_2_out, curr_state[1], register_2_q);
  and and_3 (and_3_out, curr_state[1], curr_state[0], not_4_out);
  and and_4 (and_4_out, curr_state[2], not_3_out, register_3_q);
  and and_5 (and_5_out, not_1_out, not_2_out, register_2_q);
  and and_6 (and_6_out, not_1_out, not_2_out, curr_state[0], not_4_out, register_3_q);
  or or_1 (next_state[1], and_5_out, and_6_out, and_7_out);
  and and_7 (and_7_out, curr_state[1], not_3_out, register_3_q);
  and and_8 (and_8_out, not_3_out, register_3_q);
  and and_9 (and_9_out, not_1_out, not_2_out, not_3_out, register_1_q);
  and and_10 (and_10_out, not_1_out, not_2_out, curr_state[0], not_4_out, not_6_out);
  and and_11 (and_11_out, not_1_out, curr_state[0], register_2_q);
  and and_12 (and_12_out, curr_state[0], register_1_q);
  and and_13 (and_13_out, curr_state[1], register_1_q);
  and and_14 (and_14_out, curr_state[2], not_2_out, register_2_q);
  and and_15 (and_15_out, curr_state[2], register_1_q);
  and and_16 (and_16_out, curr_state[2], curr_state[0], register_3_q);
  and and_17 (and_17_out, curr_state[2], curr_state[0], register_2_q);
  and and_18 (and_18_out, curr_state[2], curr_state[1], not_6_out);
  and and_19 (and_19_out, curr_state[1], curr_state[0], register_1_q);
  and and_20 (and_20_out, curr_state[2], register_1_q);
  or or_2 (dime_out, and_19_out, and_20_out, and_21_out);
  and and_21 (and_21_out, curr_state[2], curr_state[1], curr_state[0], not_5_out, not_6_out);
  and and_22 (and_22_out, curr_state[1], not_3_out, register_1_q);
  and and_23 (and_23_out, curr_state[2], register_1_q);
  and and_24 (and_24_out, curr_state[2], curr_state[0], register_2_q, not_6_out);
  and and_25 (and_25_out, curr_state[2], curr_state[1], curr_state[0], not_6_out);
  or or_3 (next_state[2], and_1_out, and_2_out, and_3_out, and_4_out);
  or or_4 (next_state[0], and_8_out, and_9_out, and_10_out, and_11_out);
  or or_5 (dispense, and_12_out, and_13_out, and_14_out, and_15_out, and_16_out, and_17_out, and_18_out);
  or or_6 (nickel_out, and_22_out, and_23_out, and_24_out, and_25_out);

  // Other names for the same wires on the sheet: clk = ClkIn; DimeReceieved = DimeReceivedIn; Enable = EnableIn;
  //   NickelReceieved = NickelReceivedIn; QuarterReceieved = QuarterReceivedIn
endmodule
